# Fritzing sketch blepowermon-fritzing (saved by Fritzing 0.9.6b)
circuit board: 8.46667cm x 5.64444cm
breadboards: 1

parts:
  Part2 = Adafruit HUZZAH32 ESP32 Feather [part_number="Adafruit #3405"]
  Squix1 = OLED 0.96" 128x64 I2C SSD1306
  R1 = Resistor [tolerance=±5% resistance=220 power=0.25 package=THT]
  R2 = Resistor [tolerance=±5% resistance=220 power=0.25 package=THT]
  J1 = Screw terminal - 2 pins [package=THT]
  Part3 = Adafruit ADS1115 16Bit I2C ADC [part_number="Adafruit #1085"]
  R3 = Resistor [tolerance=±5% resistance=270k power=0.25 package=THT]
  R4 = Resistor [tolerance=±5% resistance=270k power=0.25 package=THT]
  R5 = Resistor [tolerance=±5% resistance=39 power=0.25 package=THT]
  C1 = Ceramic Capacitor [capacitance=100nF voltage=35V package="100 mil [THT, multilayer]"]

nets:
  GND: Part2.GND, Squix1.GND, Part3.ADDR, Part3.GND, R4.Pin_1, C1.0
  3.3V: Part2.3.3V, Squix1.VCC, R1.Pin_1, R2.Pin_1, Part3.VDD, R3.Pin_0
  N1: Part2.SCL, Squix1.SCL, R2.Pin_0, Part3.SCL
  N2: Part2.SDA, Squix1.SCA, R1.Pin_0, Part3.SDA
  N3: J1.pin1, Part3.AIN0, R5.Pin_0
  N4: J1.pin2, Part3.AIN1, R3.Pin_1, R4.Pin_0, R5.Pin_1, C1.1

custom parts:
  Adafruit ADS1115 16Bit I2C ADC: For microcontrollers without an analog-to-digital converter or when you want a higher-precision ADC, the ADS1115 provides 16-bit precision at 860 samples/second over I2C. The chip can be configured as 4 single-ended input channels, or two differential channels. As a nice bonus, it even includes a programmable gain amplifier, up to x16, to help boost up smaller single/differential signals to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
